// Logisim project 流水线cpu.circ as structural Verilog: 21 circuits, main circuit main
module F_D_reg (
  input  in_1,
  input  in_2,
  input  [31:0] instr_i,
  input  [31:0] pc_i,
  input  in_5,
  output [31:0] instr_o,
  output [31:0] pc_o,
  output [31:0] pc_4_o,
  output [31:0] pc_8_o
);

  wire clk_prime, not_1_out, not_2_out;

  not not_1 (not_1_out, in_5);
  not not_2 (not_2_out, in_5);
  buf and_1 (clk_prime, in_1);  // AND_Gate
  Register #(.width(32)) register_1 (.D(instr_i), .en(not_1_out), .Q(instr_o), .clk(clk_prime), .clr(in_2));
  Register #(.width(32)) register_2 (.D(pc_i), .en(not_2_out), .Q(pc_o), .clk(clk_prime), .clr(in_2));
  Adder #(.width(32)) adder_1 (.a(pc_o), .b(32'h4), .out(pc_4_o));  // open: cin, cout
  Adder #(.width(32)) adder_2 (.a(pc_o), .b(32'h8), .out(pc_8_o));  // open: cin, cout

  // Other names for the same wires on the sheet: clk = in_1; F_D_stall = in_5; reset = in_2
endmodule

module D_E_reg (
  input  in_1,
  input  in_2,
  input  [31:0] pc_i,
  input  [31:0] RD1_i,
  input  [31:0] pc_4_i,
  input  [31:0] RD2_i,
  input  [31:0] pc_8_i,
  input  [4:0] rs_i,
  input  [31:0] EXTresult_i,
  input  [4:0] rt_i,
  input  [4:0] rd_i,
  input  [1:0] regdst,
  input  memwrite,
  input  regwrite,
  input  in_15,
  input  alusrc,
  input  memreacd,
  input  [4:0] shamt,
  input  [1:0] memtoreg,
  input  [2:0] aluctrl,
  input  [1:0] Lsel,
  input  [31:0] instr_i,
  input  [1:0] Ssel,
  output [31:0] pc_o,
  output [31:0] RD1_o,
  output [31:0] pc_4_o,
  output [31:0] RD2_o,
  output [31:0] pc_8_o,
  output [4:0] rs_o,
  output [31:0] EXTresult_o,
  output [4:0] rt_o,
  output [4:0] rd_o,
  output [1:0] out_33,
  output out_34,
  output out_35,
  output out_36,
  output [4:0] out_37,
  output out_38,
  output [1:0] out_39,
  output [2:0] out_40,
  output [1:0] out_41,
  output [31:0] out_42,
  output [1:0] out_43
);

  wire multiplexer_2_out, multiplexer_3_out, multiplexer_4_out, multiplexer_5_out;
  wire [1:0] multiplexer_1_out, multiplexer_6_out, multiplexer_8_out, multiplexer_9_out;
  wire [2:0] multiplexer_7_out;
  wire [4:0] multiplexer_12_out, multiplexer_13_out, multiplexer_14_out, multiplexer_15_out;
  wire [31:0] multiplexer_10_out, multiplexer_11_out, multiplexer_16_out, multiplexer_17_out,
       multiplexer_18_out, multiplexer_19_out, multiplexer_20_out;

  Multiplexer #(.width(2), .enable("false")) multiplexer_1 (
    .in0(regdst), .in1(2'b00), .out(multiplexer_1_out), .sel(in_15));
  Multiplexer #(.enable("false")) multiplexer_2 (.in0(memwrite), .in1(1'b0), .out(multiplexer_2_out), .sel(in_15));
  Multiplexer #(.enable("false")) multiplexer_3 (.in0(regwrite), .in1(1'b0), .out(multiplexer_3_out), .sel(in_15));
  Multiplexer #(.enable("false")) multiplexer_4 (.in0(alusrc), .in1(1'b0), .out(multiplexer_4_out), .sel(in_15));
  Multiplexer #(.enable("false")) multiplexer_5 (.in0(memreacd), .in1(1'b0), .out(multiplexer_5_out), .sel(in_15));
  Multiplexer #(.width(2), .enable("false")) multiplexer_6 (
    .in0(memtoreg), .in1(2'b00), .out(multiplexer_6_out), .sel(in_15));
  Multiplexer #(.width(3), .enable("false")) multiplexer_7 (
    .in0(aluctrl), .in1(3'b000), .out(multiplexer_7_out), .sel(in_15));
  Multiplexer #(.width(2), .enable("false")) multiplexer_8 (
    .in0(Lsel), .in1(2'b00), .out(multiplexer_8_out), .sel(in_15));
  Multiplexer #(.width(2), .enable("false")) multiplexer_9 (
    .in0(Ssel), .in1(2'b00), .out(multiplexer_9_out), .sel(in_15));
  Register #(.width(2)) register_1 (.D(multiplexer_1_out), .Q(out_33), .clk(in_1), .clr(in_2));  // open: en
  Register #(.width(1)) register_2 (.D(multiplexer_2_out), .Q(out_34), .clk(in_1), .clr(in_2));  // open: en
  Register #(.width(1)) register_3 (.D(multiplexer_3_out), .Q(out_35), .clk(in_1), .clr(in_2));  // open: en
  Register #(.width(1)) register_4 (.D(multiplexer_4_out), .Q(out_36), .clk(in_1), .clr(in_2));  // open: en
  Register #(.width(1)) register_5 (.D(multiplexer_5_out), .Q(out_38), .clk(in_1), .clr(in_2));  // open: en
  Register #(.width(2)) register_6 (.D(multiplexer_6_out), .Q(out_39), .clk(in_1), .clr(in_2));  // open: en
  Register #(.width(3)) register_7 (.D(multiplexer_7_out), .Q(out_40), .clk(in_1), .clr(in_2));  // open: en
  Register #(.width(2)) register_8 (.D(multiplexer_8_out), .Q(out_41), .clk(in_1), .clr(in_2));  // open: en
  Register #(.width(2)) register_9 (.D(multiplexer_9_out), .Q(out_43), .clk(in_1), .clr(in_2));  // open: en
  Multiplexer #(.width(32), .enable("false")) multiplexer_10 (
    .in0(RD1_i), .in1({32{1'b0}}), .out(multiplexer_10_out), .sel(in_15));
  Multiplexer #(.width(32), .enable("false")) multiplexer_11 (
    .in0(RD2_i), .in1({32{1'b0}}), .out(multiplexer_11_out), .sel(in_15));
  Multiplexer #(.width(5), .enable("false")) multiplexer_12 (
    .in0(rs_i), .in1({5{1'b0}}), .out(multiplexer_12_out), .sel(in_15));
  Multiplexer #(.width(5), .enable("false")) multiplexer_13 (
    .in0(rt_i), .in1({5{1'b0}}), .out(multiplexer_13_out), .sel(in_15));
  Multiplexer #(.width(5), .enable("false")) multiplexer_14 (
    .in0(rd_i), .in1({5{1'b0}}), .out(multiplexer_14_out), .sel(in_15));
  Register #(.width(32)) register_10 (.D(multiplexer_10_out), .Q(RD1_o), .clk(in_1), .clr(in_2));  // open: en
  Register #(.width(32)) register_11 (.D(multiplexer_11_out), .Q(RD2_o), .clk(in_1), .clr(in_2));  // open: en
  Register #(.width(5)) register_12 (.D(multiplexer_12_out), .Q(rs_o), .clk(in_1), .clr(in_2));  // open: en
  Register #(.width(5)) register_13 (.D(multiplexer_13_out), .Q(rt_o), .clk(in_1), .clr(in_2));  // open: en
  Register #(.width(5)) register_14 (.D(multiplexer_14_out), .Q(rd_o), .clk(in_1), .clr(in_2));  // open: en
  Multiplexer #(.width(5), .enable("false")) multiplexer_15 (
    .in0(shamt), .in1({5{1'b0}}), .out(multiplexer_15_out), .sel(in_15));
  Multiplexer #(.width(32), .enable("false")) multiplexer_16 (
    .in0(instr_i), .in1({32{1'b0}}), .out(multiplexer_16_out), .sel(in_15));
  Register #(.width(5)) register_15 (.D(multiplexer_15_out), .Q(out_37), .clk(in_1), .clr(in_2));  // open: en
  Register #(.width(32)) register_16 (.D(multiplexer_16_out), .Q(out_42), .clk(in_1), .clr(in_2));  // open: en
  Multiplexer #(.width(32), .enable("false")) multiplexer_17 (
    .in0(pc_i), .in1({32{1'b0}}), .out(multiplexer_17_out), .sel(in_15));
  Multiplexer #(.width(32), .enable("false")) multiplexer_18 (
    .in0(pc_4_i), .in1({32{1'b0}}), .out(multiplexer_18_out), .sel(in_15));
  Multiplexer #(.width(32), .enable("false")) multiplexer_19 (
    .in0(pc_8_i), .in1({32{1'b0}}), .out(multiplexer_19_out), .sel(in_15));
  Multiplexer #(.width(32), .enable("false")) multiplexer_20 (
    .in0(EXTresult_i), .in1({32{1'b0}}), .out(multiplexer_20_out), .sel(in_15));
  Register #(.width(32)) register_17 (.D(multiplexer_17_out), .Q(pc_o), .clk(in_1), .clr(in_2));  // open: en
  Register #(.width(32)) register_18 (.D(multiplexer_18_out), .Q(pc_4_o), .clk(in_1), .clr(in_2));  // open: en
  Register #(.width(32)) register_19 (.D(multiplexer_19_out), .Q(pc_8_o), .clk(in_1), .clr(in_2));  // open: en
  Register #(.width(32)) register_20 (.D(multiplexer_20_out), .Q(EXTresult_o), .clk(in_1), .clr(in_2));  // open: en

  // Other names for the same wires on the sheet: clk = in_1; clk_prime = in_1; flush = in_15; Reset = in_2
endmodule

module E_M_reg (
  input  in_1,
  input  in_2,
  input  memwrite,
  input  regwrite,
  input  [1:0] Lsel,
  input  memreacd,
  input  [1:0] Ssel,
  input  [1:0] memtoreg,
  input  [31:0] aluresult_i,
  input  [31:0] writedata_i,
  input  [4:0] writereg_i,
  input  [31:0] pc_i,
  input  [31:0] pc_4_i,
  input  [31:0] pc_8_i,
  input  [31:0] instr_i,
  input  [3:0] in_16,
  output out_17,
  output out_18,
  output [1:0] out_19,
  output out_20,
  output [1:0] out_21,
  output [1:0] out_22,
  output [31:0] out_23,
  output [31:0] out_24,
  output [4:0] out_25,
  output [31:0] pc_o,
  output [31:0] pc_4_o,
  output [31:0] pc_8_o,
  output [31:0] out_29,
  output [3:0] out_30
);

  wire comparator_1_lt;
  wire [3:0] multiplexer_1_out, subtractor_1_out;

  Register #(.width(1)) register_1 (.D(memwrite), .Q(out_17), .clk(in_1), .clr(in_2));  // open: en
  Register #(.width(1)) register_2 (.D(regwrite), .Q(out_18), .clk(in_1), .clr(in_2));  // open: en
  Register #(.width(1)) register_3 (.D(memreacd), .Q(out_20), .clk(in_1), .clr(in_2));  // open: en
  Register #(.width(2)) register_4 (.D(memtoreg), .Q(out_22), .clk(in_1), .clr(in_2));  // open: en
  Register #(.width(32)) register_5 (.D(aluresult_i), .Q(out_23), .clk(in_1), .clr(in_2));  // open: en
  Register #(.width(32)) register_6 (.D(writedata_i), .Q(out_24), .clk(in_1), .clr(in_2));  // open: en
  Register #(.width(5)) register_7 (.D(writereg_i), .Q(out_25), .clk(in_1), .clr(in_2));  // open: en
  Register #(.width(32)) register_8 (.D(pc_i), .Q(pc_o), .clk(in_1), .clr(in_2));  // open: en
  Register #(.width(32)) register_9 (.D(pc_4_i), .Q(pc_4_o), .clk(in_1), .clr(in_2));  // open: en
  Register #(.width(32)) register_10 (.D(pc_8_i), .Q(pc_8_o), .clk(in_1), .clr(in_2));  // open: en
  Register #(.width(32)) register_11 (.D(instr_i), .Q(out_29), .clk(in_1), .clr(in_2));  // open: en
  Subtractor #(.width(4)) subtractor_1 (.a(in_16), .b(4'b0001), .out(subtractor_1_out));  // open: bin, bout
  Comparator #(.width(4)) comparator_1 (.a(subtractor_1_out), .b(4'b0000), .lt(comparator_1_lt));  // open: gt, eq
  Multiplexer #(.width(4), .enable("false")) multiplexer_1 (
    .in0(subtractor_1_out), .in1(4'b0000), .out(multiplexer_1_out), .sel(comparator_1_lt));
  Register #(.width(4)) register_12 (.D(multiplexer_1_out), .Q(out_30), .clk(in_1), .clr(in_2));  // open: en
  Register #(.width(2)) register_13 (.D(Lsel), .Q(out_19), .clk(in_1), .clr(in_2));  // open: en
  Register #(.width(2)) register_14 (.D(Ssel), .Q(out_21), .clk(in_1), .clr(in_2));  // open: en

  // Other names for the same wires on the sheet: clk = in_1; clk_prime = in_1; Reset = in_2
endmodule

module M_W_reg (
  input  in_1,
  input  in_2,
  input  regwrite,
  input  [1:0] memtoreg,
  input  [4:0] writereg_i,
  input  [31:0] aluresult_i,
  input  [31:0] writedata_i,
  input  [31:0] readdata_i,
  input  [31:0] pc_i,
  input  [31:0] pc_4_i,
  input  [31:0] pc_8_i,
  input  [31:0] instr_i,
  input  [31:0] memaddr,
  input  [31:0] memdata,
  input  memwrite,
  input  [3:0] in_16,
  output out_17,
  output [1:0] out_18,
  output [4:0] out_19,
  output [31:0] out_20,
  output [31:0] out_21,
  output [31:0] out_22,
  output [31:0] pc_o,
  output [31:0] pc_4_o,
  output [31:0] pc_8_o,
  output [31:0] out_26,
  output [31:0] out_27,
  output [31:0] out_28,
  output out_29,
  output [3:0] out_30
);

  wire comparator_1_lt;
  wire [3:0] multiplexer_1_out, subtractor_1_out;

  Register #(.width(1)) register_1 (.D(regwrite), .Q(out_17), .clk(in_1), .clr(in_2));  // open: en
  Register #(.width(2)) register_2 (.D(memtoreg), .Q(out_18), .clk(in_1), .clr(in_2));  // open: en
  Register #(.width(5)) register_3 (.D(writereg_i), .Q(out_19), .clk(in_1), .clr(in_2));  // open: en
  Subtractor #(.width(4)) subtractor_1 (.a(in_16), .b(4'b0001), .out(subtractor_1_out));  // open: bin, bout
  Register #(.width(32)) register_4 (.D(aluresult_i), .Q(out_20), .clk(in_1), .clr(in_2));  // open: en
  Register #(.width(32)) register_5 (.D(writedata_i), .Q(out_21), .clk(in_1), .clr(in_2));  // open: en
  Register #(.width(32)) register_6 (.D(readdata_i), .Q(out_22), .clk(in_1), .clr(in_2));  // open: en
  Register #(.width(32)) register_7 (.D(pc_i), .Q(pc_o), .clk(in_1), .clr(in_2));  // open: en
  Register #(.width(32)) register_8 (.D(pc_4_i), .Q(pc_4_o), .clk(in_1), .clr(in_2));  // open: en
  Register #(.width(32)) register_9 (.D(pc_8_i), .Q(pc_8_o), .clk(in_1), .clr(in_2));  // open: en
  Register #(.width(32)) register_10 (.D(instr_i), .Q(out_26), .clk(in_1), .clr(in_2));  // open: en
  Register #(.width(32)) register_11 (.D(memaddr), .Q(out_27), .clk(in_1), .clr(in_2));  // open: en
  Register #(.width(32)) register_12 (.D(memdata), .Q(out_28), .clk(in_1), .clr(in_2));  // open: en
  Register #(.width(1)) register_13 (.D(memwrite), .Q(out_29), .clk(in_1), .clr(in_2));  // open: en
  Comparator #(.width(4)) comparator_1 (.a(subtractor_1_out), .b(4'b0000), .lt(comparator_1_lt));  // open: gt, eq
  Multiplexer #(.width(4), .enable("false")) multiplexer_1 (
    .in0(subtractor_1_out), .in1(4'b0000), .out(multiplexer_1_out), .sel(comparator_1_lt));
  Register #(.width(4)) register_14 (.D(multiplexer_1_out), .Q(out_30), .clk(in_1), .clr(in_2));  // open: en

  // Other names for the same wires on the sheet: clk = in_1; clk_prime = in_1; Reset = in_2
endmodule

module main (
  input  in_1,
  output [31:0] Instr,
  output regWrite,
  output [4:0] RegAddr,
  output [31:0] Regdata,
  output memWrite,
  output [4:0] MemAddr,
  output [31:0] MemData
);

  wire AluSrc, beq, Clk, DEC_EXE_out_34, DEC_EXE_out_35, DEC_EXE_out_36, EXE_MEM_out_17, EXE_MEM_out_18,
       flush_E, forwardunit_1_frtmsel, j, jal, jr, MemWrite_t, RegWrite_t, stall_D, stall_F, zero;
  wire [1:0] Bsel, d_1_tuse1_d, d_1_tuse2_d, DEC_EXE_out_33, DEC_EXE_out_39, DEC_EXE_out_41, DEC_EXE_out_43,
       EXE_MEM_out_19, EXE_MEM_out_21, EXE_MEM_out_22, ExtOp, forwardunit_1_frsdsel, forwardunit_1_frsesel,
       forwardunit_1_frtdsel, forwardunit_1_frtesel, MEM_WB_out_18, MemtoReg, RegDst, Ssel;
  wire [2:0] AluOp, DEC_EXE_out_40, npcop;
  wire [3:0] e_1_tnew_e, EXE_MEM_out_30, MEM_WB_out_30;
  wire [4:0] d_1_s1_d, d_1_s2_d, DEC_EXE_out_37, DEC_EXE_rd_o, e_1_des_e, e_1_s1_e, e_1_s2_e, EXE_MEM_out_25,
       m_1_des_e, m_1_s2_e, multiplexer_4_out, s1_d, s1_e, s2_d, s2_e, shamt, splitter__15_11, w_1_des_e;
  wire [5:0] splitter__5_0, splitter__31_26;
  wire [9:0] pc_1_out_5;
  wire [15:0] IF_DEC_instr_o, splitter_out_7;
  wire [31:0] alu_1_out_5, alu_w, bit_extender_1_out, D_CMP_RS, D_CMP_RT, DEC_EXE_extresult_o,
       DEC_EXE_out_42, DEC_EXE_pc_4_o, DEC_EXE_pc_8_o, DEC_EXE_pc_o, dm_1_rd, E_ALU_A, E_ALU_B, EtoD,
       EXE_MEM_out_23, EXE_MEM_out_24, EXE_MEM_out_29, EXE_MEM_pc_4_o, EXE_MEM_pc_8_o, EXE_MEM_pc_o,
       extresult, IF_DEC_pc_4_o, IF_DEC_pc_8_o, IF_DEC_pc_o, instr_w, M_DM_WD, MEM_WB_out_22, MemAddr_t,
       MtoD, multiplexer_2_out, npc_1_out_7, pc_1_out_6, pc_8_w, rd1, rd2, rs_e, rt_e, WtoD;
  wire [31:16] IF_DEC_instr_o_2;

  // Probe on npc_1_out_7
  Clock clock_1 (.out(Clk));
  PC pc_1 (.in_3(npc_1_out_7), .out_5(pc_1_out_5), .Clk(Clk), .reset(in_1), .stallF(stall_F), .out_6(pc_1_out_6));
  // Probe on pc_1_out_6
  // Probe on pc_1_out_5
  assign bit_extender_1_out = {{14{IF_DEC_instr_o[15]}}, {IF_DEC_instr_o, 2'b00}};  // Bit_Extender bit_extender_1
  ROM #(.addrWidth(10), .dataWidth(32)) rom_1 (.addr(pc_1_out_5), .data(Instr));  // open: sel
  NPC npc_1 (
    .out_7(npc_1_out_7), .in_3(npcop), .pc(pc_1_out_6), .str({IF_DEC_instr_o_2, IF_DEC_instr_o}),
    .extend(bit_extender_1_out), .rs(D_CMP_RS), .zero(zero));
  F_D_reg IF_DEC (
    .instr_i(Instr), .pc_i(pc_1_out_6), .instr_o({IF_DEC_instr_o_2, IF_DEC_instr_o}), .pc_o(IF_DEC_pc_o),
    .in_1(Clk), .in_2(in_1), .in_5(stall_D), .pc_4_o(IF_DEC_pc_4_o), .pc_8_o(IF_DEC_pc_8_o));
  // Probe on {IF_DEC_instr_o_2, IF_DEC_instr_o}
  splitter splitter (
    .in_1({IF_DEC_instr_o_2, IF_DEC_instr_o}), ._31_26(splitter__31_26), ._5_0(splitter__5_0), ._25_21(s1_d),
    ._20_16(s2_d), ._15_11(splitter__15_11), .out_7(splitter_out_7), .out_8(shamt));
  EXT ext_1 (.in_1(splitter_out_7), .in_2(ExtOp), .out_3(extresult));
  Control control_1 (
    .out_3(RegDst), .DMWr_MemWrite(MemWrite_t), .Branch_beq(beq), .Branch_jal(jal), .Branch_j(j),
    .Branch_jr(jr), .EXTOp(ExtOp), .RFWr_RegWrite(RegWrite_t), .BSel_M3__AluSrc(AluSrc), .out_12(MemtoReg),
    .ALUOp(AluOp), .Ssel(Ssel), .Lsel(Bsel), .in_1(splitter__31_26), .Func(splitter__5_0));
  D d_1 (
    .Instr_D({IF_DEC_instr_o_2, IF_DEC_instr_o}), .S1_D(d_1_s1_d), .S2_D(d_1_s2_d), .tuse1_D(d_1_tuse1_d),
    .tuse2_D(d_1_tuse2_d));
  E e_1 (
    .Instr_D(DEC_EXE_out_42), .extresult(DEC_EXE_extresult_o), .pc_8(DEC_EXE_pc_8_o), .S1_E(e_1_s1_e),
    .S2_E(e_1_s2_e), .Tnew_E(e_1_tnew_e), .EtoD(EtoD), .des_E(e_1_des_e));
  M m_1 (
    .Instr_D(EXE_MEM_out_29), .aluresult(EXE_MEM_out_23), .pc_8(EXE_MEM_pc_8_o), .S2_E(m_1_s2_e),
    .EtoD(MtoD), .des_E(m_1_des_e));
  W w_1 (.Instr_D(instr_w), .aluresult(alu_w), .pc_8(pc_8_w), .RegData(Regdata), .EtoD(WtoD), .des_E(w_1_des_e));
  GRF grf_1 (
    .A1(s1_d), .A2(s2_d), .A3(RegAddr), .WD(Regdata), .clk(Clk), .reset(in_1), .we(regWrite), .RD1(rd1),
    .RD2(rd2));
  NpcOp npcop_1 (.beq(beq), .j(j), .jal(jal), .jr(jr), .out_5(npcop));
  // Probe on d_1_tuse1_d
  // Probe on d_1_tuse2_d
  Comparator #(.width(32)) comparator_1 (.a(D_CMP_RS), .b(D_CMP_RT), .eq(zero));  // open: gt, lt
  StallUnit stallunit_1 (
    .s1_D(d_1_s1_d), .s2_D(d_1_s2_d), .tUse1_D(d_1_tuse1_d), .tUse2_D(d_1_tuse2_d), .des_E(e_1_des_e),
    .tNew_E(e_1_tnew_e), .tNew_M(EXE_MEM_out_30), .des_M(m_1_des_e), .Stall_F(stall_F), .Stall_D(stall_D),
    .flush_E(flush_E));
  Multiplexer #(.select(2), .width(32), .enable("false")) multiplexer_1 (
    .in0(rd1), .in1(EtoD), .in2(MtoD), .in3({32{1'b0}}), .out(D_CMP_RS), .sel(forwardunit_1_frsdsel));
  D_E_reg DEC_EXE (
    .pc_i(IF_DEC_pc_o), .RD1_i(D_CMP_RS), .pc_4_i(IF_DEC_pc_4_o), .RD2_i(D_CMP_RT), .pc_8_i(IF_DEC_pc_8_o),
    .rs_i(s1_d), .EXTresult_i(extresult), .rt_i(s2_d), .rd_i(splitter__15_11), .pc_o(DEC_EXE_pc_o),
    .RD1_o(rs_e), .pc_4_o(DEC_EXE_pc_4_o), .RD2_o(rt_e), .pc_8_o(DEC_EXE_pc_8_o), .rs_o(s1_e),
    .EXTresult_o(DEC_EXE_extresult_o), .rt_o(s2_e), .rd_o(DEC_EXE_rd_o), .in_1(Clk), .in_2(in_1),
    .in_15(flush_E), .memwrite(MemWrite_t), .out_34(DEC_EXE_out_34), .regwrite(RegWrite_t),
    .out_35(DEC_EXE_out_35), .alusrc(AluSrc), .out_36(DEC_EXE_out_36), .regdst(RegDst),
    .out_33(DEC_EXE_out_33), .aluctrl(AluOp), .out_40(DEC_EXE_out_40), .memtoreg(MemtoReg),
    .out_39(DEC_EXE_out_39), .instr_i({IF_DEC_instr_o_2, IF_DEC_instr_o}), .out_42(DEC_EXE_out_42),
    .Lsel(Bsel), .out_41(DEC_EXE_out_41), .Ssel(Ssel), .out_43(DEC_EXE_out_43), .out_37(DEC_EXE_out_37),
    .shamt(shamt));  // open: memreacd, out_38
  Multiplexer #(.width(32), .enable("false")) multiplexer_2 (
    .in0(E_ALU_B), .in1(DEC_EXE_extresult_o), .out(multiplexer_2_out), .sel(DEC_EXE_out_36));
  Multiplexer #(.select(2), .width(32), .enable("false")) multiplexer_3 (
    .in0(rd2), .in1(EtoD), .in2(MtoD), .in3({32{1'b0}}), .out(D_CMP_RT), .sel(forwardunit_1_frtdsel));
  Multiplexer #(.select(2), .width(5), .enable("false")) multiplexer_4 (
    .in0(s2_e), .in1(DEC_EXE_rd_o), .in2({5{1'b1}}), .out(multiplexer_4_out), .sel(DEC_EXE_out_33));  // open: in3
  forwardUnit forwardunit_1 (
    .s1_D(d_1_s1_d), .s2_D(d_1_s2_d), .s1_E(e_1_s1_e), .s2_E(e_1_s2_e), .des_E(e_1_des_e),
    .tNew_E(e_1_tnew_e), .s2_M(m_1_s2_e), .tNew_M(EXE_MEM_out_30), .des_M(m_1_des_e), .tNew_W(MEM_WB_out_30),
    .des_W(w_1_des_e), .fRsDsel(forwardunit_1_frsdsel), .fRtDsel(forwardunit_1_frtdsel),
    .fRsEsel(forwardunit_1_frsesel), .fRtEsel(forwardunit_1_frtesel), .fRtMsel(forwardunit_1_frtmsel));
  ALU alu_1 (
    .in_1(E_ALU_A), .in_2(multiplexer_2_out), .in_4(DEC_EXE_out_40), .out_5(alu_1_out_5),
    .shamt(DEC_EXE_out_37));
  Multiplexer #(.select(2), .width(32), .enable("false")) multiplexer_5 (
    .in0(rs_e), .in1(MtoD), .in2(WtoD), .in3({32{1'b0}}), .out(E_ALU_A), .sel(forwardunit_1_frsesel));
  E_M_reg EXE_MEM (
    .memwrite(DEC_EXE_out_34), .regwrite(DEC_EXE_out_35), .memtoreg(DEC_EXE_out_39),
    .aluresult_i(alu_1_out_5), .writedata_i(E_ALU_B), .writereg_i(multiplexer_4_out), .pc_i(DEC_EXE_pc_o),
    .pc_4_i(DEC_EXE_pc_4_o), .pc_8_i(DEC_EXE_pc_8_o), .out_17(EXE_MEM_out_17), .out_18(EXE_MEM_out_18),
    .out_22(EXE_MEM_out_22), .out_23(EXE_MEM_out_23), .out_24(EXE_MEM_out_24), .out_25(EXE_MEM_out_25),
    .pc_o(EXE_MEM_pc_o), .pc_4_o(EXE_MEM_pc_4_o), .pc_8_o(EXE_MEM_pc_8_o), .in_1(Clk), .in_2(in_1),
    .instr_i(DEC_EXE_out_42), .out_29(EXE_MEM_out_29), .in_16(e_1_tnew_e), .out_30(EXE_MEM_out_30),
    .Lsel(DEC_EXE_out_41), .out_19(EXE_MEM_out_19), .Ssel(DEC_EXE_out_43), .out_21(EXE_MEM_out_21));  // open: memreacd, out_20
  // Probe on EXE_MEM_out_30
  // Probe on e_1_tnew_e
  Multiplexer #(.select(2), .width(32), .enable("false")) multiplexer_6 (
    .in0(rt_e), .in1(MtoD), .in2(WtoD), .in3({32{1'b0}}), .out(E_ALU_B), .sel(forwardunit_1_frtesel));
  DM dm_1 (
    .SSel(EXE_MEM_out_21), .LSel(EXE_MEM_out_19), .A(EXE_MEM_out_23), .RD(dm_1_rd), .WD(M_DM_WD),
    .DMWr(EXE_MEM_out_17), .clk(Clk), .reset(in_1));
  // Probe on WtoD
  Multiplexer #(.width(32), .enable("false")) multiplexer_7 (
    .in0(EXE_MEM_out_24), .in1(WtoD), .out(M_DM_WD), .sel(forwardunit_1_frtmsel));
  M_W_reg MEM_WB (
    .regwrite(EXE_MEM_out_18), .memtoreg(EXE_MEM_out_22), .aluresult_i(EXE_MEM_out_23),
    .writedata_i(EXE_MEM_out_24), .readdata_i(dm_1_rd), .pc_i(EXE_MEM_pc_o), .pc_4_i(EXE_MEM_pc_4_o),
    .pc_8_i(EXE_MEM_pc_8_o), .out_17(regWrite), .out_18(MEM_WB_out_18), .out_20(alu_w),
    .out_22(MEM_WB_out_22), .pc_8_o(pc_8_w), .in_1(Clk), .in_2(in_1), .instr_i(EXE_MEM_out_29),
    .out_26(instr_w), .writereg_i(EXE_MEM_out_25), .out_19(RegAddr), .memaddr(EXE_MEM_out_23),
    .out_27({MemAddr_t[31:7], MemAddr, MemAddr_t[1:0]}), .memdata(M_DM_WD), .out_28(MemData),
    .memwrite(EXE_MEM_out_17), .out_29(memWrite), .out_30(MEM_WB_out_30), .in_16(EXE_MEM_out_30));  // open: out_21, pc_o, pc_4_o
  Multiplexer #(.select(2), .width(32), .enable("false")) multiplexer_8 (
    .in0(alu_w), .in1(MEM_WB_out_22), .in2(pc_8_w), .out(Regdata), .sel(MEM_WB_out_18));  // open: in3

  // Other names for the same wires on the sheet: MemAddr_t[6:2] = MemAddr; reset = in_1

  // Notes on the sheet:
  //   contents of rom_1 (hex, n*v repeats v):
  //   36100008 35080001 35290001 12080008 0 0 ae290000 25080001 26310004 94840 8000c03 0 c
endmodule

module GRF (
  input  [4:0] A1,
  input  clk,
  input  reset,
  input  we,
  input  [4:0] A2,
  input  [4:0] A3,
  input  [31:0] WD,
  output [31:0] RD1,
  output [31:0] RD2
);

  wire and_1_out, and_2_out, comparator_1_eq, comparator_2_eq, comparator_3_eq, comparator_4_eq;
  wire [31:0] I0, I1, I2, I3, I4, I5, I6, I7, I8, I9, I10, I11, I12, I13, I14, I15, I16, I17, I18, I19, I20,
       I21, I22, I23, I24, I25, I26, I27, I28, I29, I30, I31, multiplexer_3_out, multiplexer_4_out, O0, O1,
       O2, O3, O4, O5, O6, O7, O8, O9, O10, O11, O12, O13, O14, O15, O16, O17, O18, O19, O20, O21, O22, O23,
       O24, O25, O26, O27, O28, O29, O30, O31, RD1_t, RD2_t;

  Demultiplexer #(.select(5), .width(32), .tristate("true")) demultiplexer_1 (
    .out0(I0), .out1(I1), .out2(I2), .out3(I3), .out4(I4), .out5(I5), .out6(I6), .out7(I7), .out8(I8),
    .out9(I9), .out10(I10), .out11(I11), .out12(I12), .out13(I13), .out14(I14), .out15(I15), .out16(I16),
    .out17(I17), .out18(I18), .out19(I19), .out20(I20), .out21(I21), .out22(I22), .out23(I23), .out24(I24),
    .out25(I25), .out26(I26), .out27(I27), .out28(I28), .out29(I29), .out30(I30), .out31(I31), .in(WD),
    .sel(A3));  // open: en
  Multiplexer #(.select(5), .width(32)) multiplexer_1 (
    .in0(O0), .in1(O1), .in2(O2), .in3(O3), .in4(O4), .in5(O5), .in6(O6), .in7(O7), .in8(O8), .in9(O9),
    .in10(O10), .in11(O11), .in12(O12), .in13(O13), .in14(O14), .in15(O15), .in16(O16), .in17(O17),
    .in18(O18), .in19(O19), .in20(O20), .in21(O21), .in22(O22), .in23(O23), .in24(O24), .in25(O25),
    .in26(O26), .in27(O27), .in28(O28), .in29(O29), .in30(O30), .in31(O31), .out(RD2_t), .sel(A2));  // open: en
  Comparator #(.width(5)) comparator_1 (.a(A1), .b({5{1'b0}}), .eq(comparator_1_eq));  // open: gt, lt
  Comparator #(.width(5)) comparator_2 (.a(A1), .b(A3), .eq(comparator_2_eq));  // open: gt, lt
  Comparator #(.width(5)) comparator_3 (.a(A2), .b({5{1'b0}}), .eq(comparator_3_eq));  // open: gt, lt
  Comparator #(.width(5)) comparator_4 (.a(A2), .b(A3), .eq(comparator_4_eq));  // open: gt, lt
  Multiplexer #(.select(5), .width(32)) multiplexer_2 (
    .in0(O0), .in1(O1), .in2(O2), .in3(O3), .in4(O4), .in5(O5), .in6(O6), .in7(O7), .in8(O8), .in9(O9),
    .in10(O10), .in11(O11), .in12(O12), .in13(O13), .in14(O14), .in15(O15), .in16(O16), .in17(O17),
    .in18(O18), .in19(O19), .in20(O20), .in21(O21), .in22(O22), .in23(O23), .in24(O24), .in25(O25),
    .in26(O26), .in27(O27), .in28(O28), .in29(O29), .in30(O30), .in31(O31), .out(RD1_t), .sel(A1));  // open: en
  and and_1 (and_1_out, comparator_2_eq, we);
  and and_2 (and_2_out, comparator_4_eq, we);
  Multiplexer #(.width(32), .enable("false")) multiplexer_3 (
    .in0(RD1_t), .in1(WD), .out(multiplexer_3_out), .sel(and_1_out));
  Multiplexer #(.width(32), .enable("false")) multiplexer_4 (
    .in0(RD2_t), .in1(WD), .out(multiplexer_4_out), .sel(and_2_out));
  Multiplexer #(.width(32), .enable("false")) multiplexer_5 (
    .in0(multiplexer_3_out), .in1({32{1'b0}}), .out(RD1), .sel(comparator_1_eq));
  Multiplexer #(.width(32), .enable("false")) multiplexer_6 (
    .in0(multiplexer_4_out), .in1({32{1'b0}}), .out(RD2), .sel(comparator_3_eq));
  Register #(.width(32)) register_1 (.D({32{1'b0}}), .en(we), .Q(O0), .clk(clk), .clr(reset));
  Register #(.width(32)) register_2 (.D(I8), .en(we), .Q(O8), .clk(clk), .clr(reset));
  Register #(.width(32)) register_3 (.D(I16), .en(we), .Q(O16), .clk(clk), .clr(reset));
  Register #(.width(32)) register_4 (.D(I24), .en(we), .Q(O24), .clk(clk), .clr(reset));
  Register #(.width(32)) register_5 (.D(I1), .en(we), .Q(O1), .clk(clk), .clr(reset));
  Register #(.width(32)) register_6 (.D(I9), .en(we), .Q(O9), .clk(clk), .clr(reset));
  Register #(.width(32)) register_7 (.D(I17), .en(we), .Q(O17), .clk(clk), .clr(reset));
  Register #(.width(32)) register_8 (.D(I25), .en(we), .Q(O25), .clk(clk), .clr(reset));
  Register #(.width(32)) register_9 (.D(I2), .en(we), .Q(O2), .clk(clk), .clr(reset));
  Register #(.width(32)) register_10 (.D(I10), .en(we), .Q(O10), .clk(clk), .clr(reset));
  Register #(.width(32)) register_11 (.D(I18), .en(we), .Q(O18), .clk(clk), .clr(reset));
  Register #(.width(32)) register_12 (.D(I26), .en(we), .Q(O26), .clk(clk), .clr(reset));
  Register #(.width(32)) register_13 (.D(I3), .en(we), .Q(O3), .clk(clk), .clr(reset));
  Register #(.width(32)) register_14 (.D(I11), .en(we), .Q(O11), .clk(clk), .clr(reset));
  Register #(.width(32)) register_15 (.D(I19), .en(we), .Q(O19), .clk(clk), .clr(reset));
  Register #(.width(32)) register_16 (.D(I27), .en(we), .Q(O27), .clk(clk), .clr(reset));
  Register #(.width(32)) register_17 (.D(I4), .en(we), .Q(O4), .clk(clk), .clr(reset));
  Register #(.width(32)) register_18 (.D(I12), .en(we), .Q(O12), .clk(clk), .clr(reset));
  Register #(.width(32)) register_19 (.D(I20), .en(we), .Q(O20), .clk(clk), .clr(reset));
  Register #(.width(32)) register_20 (.D(I28), .en(we), .Q(O28), .clk(clk), .clr(reset));
  Register #(.width(32)) register_21 (.D(I5), .en(we), .Q(O5), .clk(clk), .clr(reset));
  Register #(.width(32)) register_22 (.D(I13), .en(we), .Q(O13), .clk(clk), .clr(reset));
  Register #(.width(32)) register_23 (.D(I21), .en(we), .Q(O21), .clk(clk), .clr(reset));
  Register #(.width(32)) register_24 (.D(I29), .en(we), .Q(O29), .clk(clk), .clr(reset));
  Register #(.width(32)) register_25 (.D(I6), .en(we), .Q(O6), .clk(clk), .clr(reset));
  Register #(.width(32)) register_26 (.D(I14), .en(we), .Q(O14), .clk(clk), .clr(reset));
  Register #(.width(32)) register_27 (.D(I22), .en(we), .Q(O22), .clk(clk), .clr(reset));
  Register #(.width(32)) register_28 (.D(I30), .en(we), .Q(O30), .clk(clk), .clr(reset));
  Register #(.width(32)) register_29 (.D(I7), .en(we), .Q(O7), .clk(clk), .clr(reset));
  Register #(.width(32)) register_30 (.D(I15), .en(we), .Q(O15), .clk(clk), .clr(reset));
  Register #(.width(32)) register_31 (.D(I23), .en(we), .Q(O23), .clk(clk), .clr(reset));
  Register #(.width(32)) register_32 (.D(I31), .en(we), .Q(O31), .clk(clk), .clr(reset));
endmodule

module splitter (
  input  [31:0] in_1,
  output [5:0] _31_26,
  output [5:0] _5_0,
  output [4:0] _25_21,
  output [4:0] _20_16,
  output [4:0] _15_11,
  output [15:0] out_7,
  output [4:0] out_8
);


  assign _5_0 = in_1[5:0];
  assign _15_11 = in_1[15:11];
  assign _20_16 = in_1[20:16];
  assign _25_21 = in_1[25:21];
  assign _31_26 = in_1[31:26];
  assign out_7 = in_1[15:0];
  assign out_8 = in_1[10:6];

  // Notes on the sheet:
  //   IM.D
  //   15~00
endmodule

module EXT (
  input  [15:0] in_1,
  input  [1:0] in_2,
  output [31:0] out_3
);

  wire [31:0] bit_extender_1_out, bit_extender_2_out;

  assign bit_extender_1_out = {{16{1'b0}}, in_1};  // Bit_Extender bit_extender_1
  assign bit_extender_2_out = {{16{in_1[15]}}, in_1};  // Bit_Extender bit_extender_2
  Multiplexer #(.select(2), .width(32), .enable("false")) multiplexer_1 (
    .in0(bit_extender_1_out), .in1(bit_extender_2_out), .in2({in_1, {16{1'b0}}}), .out(out_3), .sel(in_2));  // open: in3

  // Notes on the sheet:
  //   IMM16
  //   EXTOp
endmodule

module ALU (
  input  [31:0] in_1,
  input  [31:0] in_2,
  input  [4:0] shamt,
  input  [2:0] in_4,
  output [31:0] out_5
);

  wire [31:0] adder_1_out, or_1_out, shifter_1_out, subtractor_1_out;

  Subtractor #(.width(32)) subtractor_1 (.a(in_1), .b(in_2), .out(subtractor_1_out));  // open: bin, bout
  Adder #(.width(32)) adder_1 (.a(in_1), .b(in_2), .out(adder_1_out));  // open: cin, cout
  Shifter #(.width(32)) shifter_1 (.in(in_2), .\dist (shamt), .out(shifter_1_out));
  assign or_1_out = in_1 | in_2;  // OR_Gate or_1, 32 bits wide
  Multiplexer #(.select(3), .width(32), .enable("false")) multiplexer_1 (
    .in1(adder_1_out), .in2(subtractor_1_out), .in3(or_1_out), .in4(shifter_1_out), .out(out_5), .sel(in_4));  // open: in0, in5, in6, in7

  // Notes on the sheet:
  //   01：无溢出加法
  //   10：无溢出减法
  //   11：ori
  //   100：sll
endmodule

module Control (
  input  [5:0] in_1,
  input  [5:0] Func,
  output [1:0] out_3,
  output DMWr_MemWrite,
  output Branch_beq,
  output Branch_jal,
  output Branch_j,
  output Branch_jr,
  output [1:0] EXTOp,
  output RFWr_RegWrite,
  output BSel_M3__AluSrc,
  output [1:0] out_12,
  output [2:0] ALUOp,
  output [1:0] Ssel,
  output [1:0] Lsel
);

  wire addiu, addu, bne, lui, lw, nop, or_1_out, or_2_out, or_3_out, or_4_out, or_5_out, or_6_out, or_7_out,
       or_8_out, or_9_out, or_10_out, or_11_out, or_12_out, or_13_out, or_14_out, ori, sll, subu, sw;
  wire [1:0] multiplexer_2_out, multiplexer_3_out, multiplexer_4_out, multiplexer_5_out, multiplexer_6_out;
  wire [2:0] multiplexer_7_out, multiplexer_8_out, multiplexer_9_out, multiplexer_10_out;

  control_part control_part_1 (
    .out_3(addu), .out_4(subu), .out_5(Branch_jr), .out_6(nop), .out_8(lw), .out_9(sw), .out_10(ori),
    .out_11(Branch_j), .out_12(Branch_beq), .out_13(Branch_jal), .out_14(addiu), .out_15(bne), .out_16(lui),
    .out_17(Lsel[0]), .out_18(Lsel[1]), .out_19(Ssel[0]), .out_20(Ssel[1]), .OP(in_1), .Func(Func),
    .out_7(sll));
  or or_1 (or_1_out, ori, addiu);
  or or_2 (or_2_out, Lsel[0], Ssel[1], Lsel[1], Ssel[0], sw, lw);
  or or_3 (or_3_out, addu, subu, sll);
  or or_4 (or_4_out, addiu, sw, lw, Ssel[0], Ssel[1], Lsel[0], Lsel[1]);
  or or_5 (or_5_out, lw, Lsel[0], Lsel[1]);
  or or_6 (or_6_out, addu, lui, subu, addiu, ori);
  or or_7 (or_7_out, Lsel[0], Lsel[1], lw);
  buf or_8 (or_8_out, Branch_jal);  // OR_Gate
  or or_9 (or_9_out, or_2_out, lui, addiu, addu);
  buf or_10 (or_10_out, subu);  // OR_Gate
  Multiplexer #(.enable("false")) multiplexer_1 (.in0(1'b0), .in1(1'b1), .out(out_3[0]), .sel(or_3_out));
  Multiplexer #(.width(2), .enable("false")) multiplexer_2 (
    .in0(2'b00), .in1(2'b01), .out(multiplexer_2_out), .sel(or_4_out));
  Multiplexer #(.width(2), .enable("false")) multiplexer_3 (
    .in0(2'b00), .in1(2'b10), .out(multiplexer_3_out), .sel(lui));
  or or_11 (or_11_out, addu, sll, subu);
  or or_12 (or_12_out, Branch_beq, sll, addu, bne, subu);
  Multiplexer #(.width(2), .enable("false")) multiplexer_4 (
    .in0(2'b00), .in1(2'b00), .out(multiplexer_4_out), .sel(or_6_out));
  Multiplexer #(.width(2), .enable("false")) multiplexer_5 (
    .in0(2'b00), .in1(2'b01), .out(multiplexer_5_out), .sel(or_7_out));
  Multiplexer #(.width(2), .enable("false")) multiplexer_6 (
    .in0(2'b00), .in1(2'b10), .out(multiplexer_6_out), .sel(or_8_out));
  Multiplexer #(.width(3), .enable("false")) multiplexer_7 (
    .in0(3'b000), .in1(3'b001), .out(multiplexer_7_out), .sel(or_9_out));
  Multiplexer #(.width(3), .enable("false")) multiplexer_8 (
    .in0(3'b000), .in1(3'b010), .out(multiplexer_8_out), .sel(or_10_out));
  Multiplexer #(.width(3), .enable("false")) multiplexer_9 (
    .in0(3'b000), .in1(3'b011), .out(multiplexer_9_out), .sel(or_13_out));
  buf or_13 (or_13_out, ori);  // OR_Gate
  Multiplexer #(.width(3), .enable("false")) multiplexer_10 (
    .in0(3'b000), .in1(3'b100), .out(multiplexer_10_out), .sel(or_14_out));
  buf or_14 (or_14_out, sll);  // OR_Gate
  or or_15 (DMWr_MemWrite, Ssel[1], sw, Ssel[0]);
  or or_16 (RFWr_RegWrite, or_11_out, lui, or_1_out, or_5_out, Branch_jal);
  Multiplexer #(.enable("false")) multiplexer_11 (.in0(1'b1), .in1(1'b0), .out(BSel_M3__AluSrc), .sel(or_12_out));
  assign EXTOp = multiplexer_2_out | multiplexer_3_out;  // OR_Gate or_17, 2 bits wide
  assign out_12 = multiplexer_4_out | multiplexer_5_out | multiplexer_6_out;  // OR_Gate or_18, 2 bits wide
  assign ALUOp = multiplexer_7_out | multiplexer_8_out | multiplexer_9_out | multiplexer_10_out;  // OR_Gate or_19, 3 bits wide

  assign out_3[1] = Branch_jal;

  // Other names for the same wires on the sheet: beq = Branch_beq; j = Branch_j; jr = Branch_jr; lb = Lsel[0];
  //   lh = Lsel[1]; jal = Branch_jal; sb = Ssel[0]; sh = Ssel[1]

  // Notes on the sheet:
  //   OP
  //   WRSel(M1)(RegDst)
  //   WDSel(M2)(MemtoReg)
endmodule

module DM (
  input  [1:0] SSel,
  input  [1:0] LSel,
  input  [31:0] A,
  input  [31:0] WD,
  input  DMWr,
  input  clk,
  input  reset,
  output [31:0] RD
);

  wire decoder_1_out0, decoder_1_out1, decoder_1_out2, decoder_1_out3, decoder_2_out0, decoder_2_out1;
  wire [7:0] _0_7, _8_15, _16_23, _24_31, multiplexer_3_out, multiplexer_4_out, multiplexer_5_out,
       multiplexer_6_out, multiplexer_8_out;
  wire [15:0] multiplexer_1_out, multiplexer_2_out, multiplexer_9_out;
  wire [31:0] bit_extender_1_out, bit_extender_2_out, multiplexer_7_out;

  Decoder #(.select(2)) decoder_1 (
    .out0(decoder_1_out0), .out1(decoder_1_out1), .out2(decoder_1_out2), .out3(decoder_1_out3), .sel(A[1:0]));  // open: en
  Decoder decoder_2 (.out0(decoder_2_out0), .out1(decoder_2_out1), .sel(A[1]));  // open: en
  Multiplexer #(.width(16)) multiplexer_1 (
    .in0({_8_15, _0_7}), .in1(WD[15:0]), .out(multiplexer_1_out), .sel(decoder_2_out0));  // open: en
  Multiplexer #(.width(16)) multiplexer_2 (
    .in0({_24_31, _16_23}), .in1(WD[15:0]), .out(multiplexer_2_out), .sel(decoder_2_out1));  // open: en
  Multiplexer #(.width(8)) multiplexer_3 (
    .in0(_0_7), .in1(WD[7:0]), .out(multiplexer_3_out), .sel(decoder_1_out0));  // open: en
  Multiplexer #(.width(8)) multiplexer_4 (
    .in0(_8_15), .in1(WD[7:0]), .out(multiplexer_4_out), .sel(decoder_1_out1));  // open: en
  Multiplexer #(.width(8)) multiplexer_5 (
    .in0(_16_23), .in1(WD[7:0]), .out(multiplexer_5_out), .sel(decoder_1_out2));  // open: en
  Multiplexer #(.width(8)) multiplexer_6 (
    .in0(_24_31), .in1(WD[7:0]), .out(multiplexer_6_out), .sel(decoder_1_out3));  // open: en
  Multiplexer #(.select(2), .width(32)) multiplexer_7 (
    .in0(WD), .in1({multiplexer_6_out, multiplexer_5_out, multiplexer_4_out, multiplexer_3_out}),
    .in2({multiplexer_2_out, multiplexer_1_out}), .out(multiplexer_7_out), .sel(SSel));  // open: in3, en
  RAM #(.addrWidth(5), .dataWidth(32), .bus("separate")) ram_1 (
    .addr(A[6:2]), .din(multiplexer_7_out), .data({_24_31, _16_23, _8_15, _0_7}), .str(DMWr), .clk(clk),
    .clr(reset));  // open: sel, ld
  Multiplexer #(.select(2), .width(8)) multiplexer_8 (
    .in0(_0_7), .in1(_8_15), .in2(_16_23), .in3(_24_31), .out(multiplexer_8_out), .sel(A[1:0]));  // open: en
  assign bit_extender_1_out = {{24{multiplexer_8_out[7]}}, multiplexer_8_out};  // Bit_Extender bit_extender_1
  assign bit_extender_2_out = {{16{multiplexer_9_out[15]}}, multiplexer_9_out};  // Bit_Extender bit_extender_2
  Multiplexer #(.width(16)) multiplexer_9 (
    .in0({_8_15, _0_7}), .in1({_24_31, _16_23}), .out(multiplexer_9_out), .sel(A[1]));  // open: en
  Multiplexer #(.select(2), .width(32)) multiplexer_10 (
    .in0({_24_31, _16_23, _8_15, _0_7}), .in1(bit_extender_1_out), .in2(bit_extender_2_out), .out(RD),
    .sel(LSel));  // open: in3, en
endmodule

module PC (
  input  Clk,
  input  reset,
  input  [31:0] in_3,
  input  stallF,
  output [9:0] out_5,
  output [31:0] out_6
);

  wire comparator_1_eq, not_1_out;
  wire [31:0] register_1_q, subtractor_1_out;

  Register #(.width(32)) register_1 (.D(in_3), .en(not_1_out), .Q(register_1_q), .clk(Clk), .clr(reset));
  not not_1 (not_1_out, stallF);
  Comparator #(.width(32)) comparator_1 (.a({32{1'b0}}), .b(register_1_q), .eq(comparator_1_eq));  // open: gt, lt
  Multiplexer #(.width(32), .enable("false")) multiplexer_1 (
    .in0(register_1_q), .in1(32'h3000), .out(out_6), .sel(comparator_1_eq));
  Subtractor #(.width(32)) subtractor_1 (
    .a(out_6), .b(32'h3000), .out({subtractor_1_out[31:12], out_5, subtractor_1_out[1:0]}));  // open: bin, bout

  // Notes on the sheet:
  //   NPC输入
  //   输出至NPC
endmodule

module NPC (
  input  zero,
  input  [31:0] pc,
  input  [2:0] in_3,
  input  [31:0] str,
  input  [31:0] extend,
  input  [31:0] rs,
  output [31:0] out_7
);

  wire [31:0] beq16, multiplexer_1_out, pc4;

  Adder #(.width(32)) adder_1 (.a(32'h4), .b(pc), .out(pc4));  // open: cin, cout
  Adder #(.width(32)) adder_2 (.a(extend), .b(pc), .out(beq16));  // open: cin, cout
  Multiplexer #(.width(32), .enable("false")) multiplexer_1 (
    .in0(pc4), .in1(beq16), .out(multiplexer_1_out), .sel(zero));
  Multiplexer #(.select(3), .width(32), .enable("false")) multiplexer_2 (
    .in0(pc4), .in1(multiplexer_1_out), .in2({pc[31:28], str[25:0], 2'b00}), .in3(rs), .out(out_7), .sel(in_3));  // open: in4, in5, in6, in7
  // Probe on out_7

  // Other names for the same wires on the sheet: j26[31:2] = {pc[31:28], str[25:0]}; jr_rs[31:0] = rs

  // Notes on the sheet:
  //   000：PC+4
  //   001：beq:
  //   010：jal_j
  //   011：jr
  //   100：bne
  //   NPC
endmodule

module forwardUnit (
  input  [4:0] s1_D,
  input  [4:0] s2_D,
  input  [4:0] s1_E,
  input  [4:0] s2_E,
  input  [4:0] des_E,
  input  [3:0] tNew_E,
  input  [4:0] s2_M,
  input  [3:0] tNew_M,
  input  [4:0] des_M,
  input  [3:0] tNew_W,
  input  [4:0] des_W,
  output [1:0] fRsDsel,
  output [1:0] fRtDsel,
  output [1:0] fRsEsel,
  output [1:0] fRtEsel,
  output fRtMsel
);

  wire and_1_out, and_2_out, and_3_out, and_4_out, and_5_out, and_6_out, and_7_out, and_8_out, and_9_out,
       comparator_1_eq, comparator_2_eq, comparator_3_eq, comparator_4_eq, comparator_5_eq, comparator_6_eq,
       comparator_7_eq, comparator_8_eq, comparator_9_eq, comparator_10_eq, comparator_11_eq,
       comparator_12_eq, comparator_13_eq, comparator_14_eq, comparator_15_eq, comparator_16_eq,
       comparator_17_eq, comparator_18_eq, comparator_19_eq, comparator_20_eq, comparator_21_eq,
       comparator_22_eq, comparator_23_eq, comparator_24_eq, comparator_25_eq, comparator_26_eq,
       comparator_27_eq, not_1_out, not_2_out, not_3_out, not_4_out, not_5_out, not_6_out, not_7_out,
       not_8_out, not_9_out;
  wire [1:0] multiplexer_1_out, multiplexer_2_out, multiplexer_5_out, multiplexer_6_out;

  Comparator #(.width(5), .mode("unsigned")) comparator_1 (
    .a(s1_D), .b({5{1'b0}}), .eq(comparator_1_eq));  // open: gt, lt
  not not_1 (not_1_out, comparator_1_eq);
  Comparator #(.width(5), .mode("unsigned")) comparator_2 (.a(s1_D), .b(des_M), .eq(comparator_2_eq));  // open: gt, lt
  Comparator #(.width(4), .mode("unsigned")) comparator_3 (
    .a(tNew_M), .b(4'b0000), .eq(comparator_3_eq));  // open: gt, lt
  not not_2 (not_2_out, comparator_4_eq);
  Comparator #(.width(5), .mode("unsigned")) comparator_4 (
    .a(s1_D), .b({5{1'b0}}), .eq(comparator_4_eq));  // open: gt, lt
  Comparator #(.width(5), .mode("unsigned")) comparator_5 (.a(s1_D), .b(des_E), .eq(comparator_5_eq));  // open: gt, lt
  Comparator #(.width(4), .mode("unsigned")) comparator_6 (
    .a(tNew_E), .b(4'b0000), .eq(comparator_6_eq));  // open: gt, lt
  Comparator #(.width(5), .mode("unsigned")) comparator_7 (
    .a(s2_D), .b({5{1'b0}}), .eq(comparator_7_eq));  // open: gt, lt
  Comparator #(.width(5), .mode("unsigned")) comparator_8 (.a(s2_D), .b(des_M), .eq(comparator_8_eq));  // open: gt, lt
  Comparator #(.width(4), .mode("unsigned")) comparator_9 (
    .a(tNew_M), .b(4'b0000), .eq(comparator_9_eq));  // open: gt, lt
  Comparator #(.width(5), .mode("unsigned")) comparator_10 (
    .a(s2_D), .b({5{1'b0}}), .eq(comparator_10_eq));  // open: gt, lt
  Comparator #(.width(5), .mode("unsigned")) comparator_11 (
    .a(s2_D), .b(des_E), .eq(comparator_11_eq));  // open: gt, lt
  Comparator #(.width(4), .mode("unsigned")) comparator_12 (
    .a(tNew_E), .b(4'b0000), .eq(comparator_12_eq));  // open: gt, lt
  and and_1 (and_1_out, not_1_out, comparator_2_eq, comparator_3_eq);
  and and_2 (and_2_out, not_2_out, comparator_5_eq, comparator_6_eq);
  not not_3 (not_3_out, comparator_7_eq);
  not not_4 (not_4_out, comparator_10_eq);
  Multiplexer #(.width(2)) multiplexer_1 (
    .in0(2'b00), .in1(2'b10), .out(multiplexer_1_out), .sel(and_1_out));  // open: en
  and and_3 (and_3_out, not_3_out, comparator_8_eq, comparator_9_eq);
  and and_4 (and_4_out, not_4_out, comparator_11_eq, comparator_12_eq);
  Multiplexer #(.width(2)) multiplexer_2 (
    .in0(2'b00), .in1(2'b10), .out(multiplexer_2_out), .sel(and_3_out));  // open: en
  Multiplexer #(.width(2)) multiplexer_3 (
    .in0(multiplexer_1_out), .in1(2'b01), .out(fRsDsel), .sel(and_2_out));  // open: en
  Multiplexer #(.width(2)) multiplexer_4 (
    .in0(multiplexer_2_out), .in1(2'b01), .out(fRtDsel), .sel(and_4_out));  // open: en
  Comparator #(.width(5), .mode("unsigned")) comparator_13 (
    .a(s1_E), .b({5{1'b0}}), .eq(comparator_13_eq));  // open: gt, lt
  Comparator #(.width(5), .mode("unsigned")) comparator_14 (
    .a(s1_E), .b(des_W), .eq(comparator_14_eq));  // open: gt, lt
  Comparator #(.width(4), .mode("unsigned")) comparator_15 (
    .a(tNew_W), .b(4'b0000), .eq(comparator_15_eq));  // open: gt, lt
  Comparator #(.width(5), .mode("unsigned")) comparator_16 (
    .a(s1_E), .b({5{1'b0}}), .eq(comparator_16_eq));  // open: gt, lt
  Comparator #(.width(5), .mode("unsigned")) comparator_17 (
    .a(s1_E), .b(des_M), .eq(comparator_17_eq));  // open: gt, lt
  Comparator #(.width(4), .mode("unsigned")) comparator_18 (
    .a(tNew_M), .b(4'b0000), .eq(comparator_18_eq));  // open: gt, lt
  Comparator #(.width(5), .mode("unsigned")) comparator_19 (
    .a(s2_E), .b({5{1'b0}}), .eq(comparator_19_eq));  // open: gt, lt
  Comparator #(.width(5), .mode("unsigned")) comparator_20 (
    .a(s2_E), .b(des_W), .eq(comparator_20_eq));  // open: gt, lt
  Comparator #(.width(4), .mode("unsigned")) comparator_21 (
    .a(tNew_W), .b(4'b0000), .eq(comparator_21_eq));  // open: gt, lt
  Comparator #(.width(5), .mode("unsigned")) comparator_22 (
    .a(s2_E), .b({5{1'b0}}), .eq(comparator_22_eq));  // open: gt, lt
  Comparator #(.width(5), .mode("unsigned")) comparator_23 (
    .a(s2_E), .b(des_M), .eq(comparator_23_eq));  // open: gt, lt
  Comparator #(.width(4), .mode("unsigned")) comparator_24 (
    .a(tNew_M), .b(4'b0000), .eq(comparator_24_eq));  // open: gt, lt
  not not_5 (not_5_out, comparator_13_eq);
  not not_6 (not_6_out, comparator_16_eq);
  not not_7 (not_7_out, comparator_19_eq);
  not not_8 (not_8_out, comparator_22_eq);
  and and_5 (and_5_out, not_5_out, comparator_14_eq, comparator_15_eq);
  and and_6 (and_6_out, not_6_out, comparator_17_eq, comparator_18_eq);
  and and_7 (and_7_out, not_7_out, comparator_20_eq, comparator_21_eq);
  and and_8 (and_8_out, not_8_out, comparator_23_eq, comparator_24_eq);
  Multiplexer #(.width(2)) multiplexer_5 (
    .in0(2'b00), .in1(2'b10), .out(multiplexer_5_out), .sel(and_5_out));  // open: en
  Multiplexer #(.width(2)) multiplexer_6 (
    .in0(2'b00), .in1(2'b10), .out(multiplexer_6_out), .sel(and_7_out));  // open: en
  Multiplexer #(.width(2)) multiplexer_7 (
    .in0(multiplexer_5_out), .in1(2'b01), .out(fRsEsel), .sel(and_6_out));  // open: en
  Multiplexer #(.width(2)) multiplexer_8 (
    .in0(multiplexer_6_out), .in1(2'b01), .out(fRtEsel), .sel(and_8_out));  // open: en
  Comparator #(.width(5), .mode("unsigned")) comparator_25 (
    .a(s2_M), .b({5{1'b0}}), .eq(comparator_25_eq));  // open: gt, lt
  not not_9 (not_9_out, comparator_25_eq);
  Comparator #(.width(5), .mode("unsigned")) comparator_26 (
    .a(s2_M), .b(des_W), .eq(comparator_26_eq));  // open: gt, lt
  Comparator #(.width(4), .mode("unsigned")) comparator_27 (
    .a(tNew_W), .b(4'b0000), .eq(comparator_27_eq));  // open: gt, lt
  and and_9 (and_9_out, not_9_out, comparator_26_eq, comparator_27_eq);
  Multiplexer multiplexer_9 (.in0(1'b0), .in1(1'b1), .out(fRtMsel), .sel(and_9_out));  // open: en
endmodule

module StallUnit (
  input  [4:0] s1_D,
  input  [4:0] s2_D,
  input  [1:0] tUse1_D,
  input  [1:0] tUse2_D,
  input  [4:0] des_E,
  input  [3:0] tNew_E,
  input  [3:0] tNew_M,
  input  [4:0] des_M,
  output Stall_F,
  output Stall_D,
  output flush_E
);

  wire and_1_out, and_2_out, and_3_out, and_4_out, comparator_1_eq, comparator_2_eq, comparator_3_lt,
       comparator_4_eq, comparator_5_eq, comparator_6_lt, comparator_7_eq, comparator_8_eq, comparator_9_lt,
       comparator_10_eq, comparator_11_eq, comparator_12_lt, not_1_out, not_2_out, not_3_out, not_4_out;
  wire [3:0] tUse1_D_t, tUse2_D_t;

  Comparator #(.width(5), .mode("unsigned")) comparator_1 (
    .a(s1_D), .b({5{1'b0}}), .eq(comparator_1_eq));  // open: gt, lt
  Comparator #(.width(5), .mode("unsigned")) comparator_2 (.a(s1_D), .b(des_E), .eq(comparator_2_eq));  // open: gt, lt
  Comparator #(.width(4), .mode("unsigned")) comparator_3 (
    .a(tUse1_D_t), .b(tNew_E), .lt(comparator_3_lt));  // open: gt, eq
  Comparator #(.width(5), .mode("unsigned")) comparator_4 (
    .a(s2_D), .b({5{1'b0}}), .eq(comparator_4_eq));  // open: gt, lt
  Comparator #(.width(5), .mode("unsigned")) comparator_5 (.a(s2_D), .b(des_E), .eq(comparator_5_eq));  // open: gt, lt
  Comparator #(.width(4), .mode("unsigned")) comparator_6 (
    .a(tUse2_D_t), .b(tNew_E), .lt(comparator_6_lt));  // open: gt, eq
  Comparator #(.width(5), .mode("unsigned")) comparator_7 (
    .a(s1_D), .b({5{1'b0}}), .eq(comparator_7_eq));  // open: gt, lt
  Comparator #(.width(5), .mode("unsigned")) comparator_8 (.a(s1_D), .b(des_M), .eq(comparator_8_eq));  // open: gt, lt
  Comparator #(.width(4), .mode("unsigned")) comparator_9 (
    .a(tUse1_D_t), .b(tNew_M), .lt(comparator_9_lt));  // open: gt, eq
  Comparator #(.width(5), .mode("unsigned")) comparator_10 (
    .a(s2_D), .b({5{1'b0}}), .eq(comparator_10_eq));  // open: gt, lt
  Comparator #(.width(5), .mode("unsigned")) comparator_11 (
    .a(s2_D), .b(des_M), .eq(comparator_11_eq));  // open: gt, lt
  Comparator #(.width(4), .mode("unsigned")) comparator_12 (
    .a(tUse2_D_t), .b(tNew_M), .lt(comparator_12_lt));  // open: gt, eq
  assign tUse1_D_t = {{2{1'b0}}, tUse1_D};  // Bit_Extender bit_extender_1
  not not_1 (not_1_out, comparator_1_eq);
  not not_2 (not_2_out, comparator_4_eq);
  not not_3 (not_3_out, comparator_7_eq);
  not not_4 (not_4_out, comparator_10_eq);
  and and_1 (and_1_out, not_1_out, comparator_2_eq, comparator_3_lt);
  and and_2 (and_2_out, not_2_out, comparator_5_eq, comparator_6_lt);
  and and_3 (and_3_out, not_3_out, comparator_8_eq, comparator_9_lt);
  and and_4 (and_4_out, not_4_out, comparator_11_eq, comparator_12_lt);
  assign tUse2_D_t = {{2{1'b0}}, tUse2_D};  // Bit_Extender bit_extender_2
  or or_1 (flush_E, and_1_out, and_2_out, and_3_out, and_4_out);

  assign Stall_D = flush_E;
  assign Stall_F = flush_E;

  // Other names for the same wires on the sheet: stall_flag = flush_E
endmodule

module control_part (
  input  [5:0] Func,
  input  [5:0] OP,
  output out_3,
  output out_4,
  output out_5,
  output out_6,
  output out_7,
  output out_8,
  output out_9,
  output out_10,
  output out_11,
  output out_12,
  output out_13,
  output out_14,
  output out_15,
  output out_16,
  output out_17,
  output out_18,
  output out_19,
  output out_20
);

  wire not_1_out, not_2_out, not_3_out, not_4_out, not_5_out, not_6_out, not_7_out, not_8_out, not_9_out,
       not_10_out, not_11_out, not_12_out, r;

  not not_1 (not_1_out, OP[5]);
  not not_2 (not_2_out, OP[3]);
  not not_3 (not_3_out, OP[4]);
  not not_4 (not_4_out, OP[2]);
  not not_5 (not_5_out, OP[0]);
  not not_6 (not_6_out, OP[1]);
  and u_r (r, not_1_out, not_3_out, not_2_out, not_4_out, not_6_out, not_5_out);
  and lw (out_8, OP[5], not_3_out, not_2_out, not_4_out, OP[1], OP[0]);
  and sw (out_9, OP[5], not_3_out, OP[3], not_4_out, OP[1], OP[0]);
  and ori (out_10, not_1_out, not_3_out, OP[3], OP[2], not_6_out, OP[0]);
  and j (out_11, not_1_out, not_3_out, not_2_out, not_4_out, OP[1], not_5_out);
  and beq (out_12, not_1_out, not_3_out, not_2_out, OP[2], not_6_out, not_5_out);
  and jal (out_13, not_1_out, not_3_out, not_2_out, not_4_out, OP[1], OP[0]);
  and addiu (out_14, not_1_out, not_3_out, OP[3], not_4_out, not_6_out, OP[0]);
  and bne (out_15, not_1_out, not_3_out, not_2_out, OP[2], not_6_out, OP[0]);
  and lui (out_16, not_1_out, not_3_out, OP[3], OP[2], OP[1], OP[0]);
  and lb (out_17, OP[5], not_3_out, not_2_out, not_4_out, not_6_out, not_5_out);
  and lh (out_18, OP[5], not_3_out, not_2_out, not_4_out, not_6_out, OP[0]);
  and sb (out_19, OP[5], not_3_out, OP[3], not_4_out, not_6_out, not_5_out);
  and sh (out_20, OP[5], not_3_out, OP[3], not_4_out, not_6_out, OP[0]);
  not not_7 (not_7_out, Func[5]);
  not not_8 (not_8_out, Func[3]);
  not not_9 (not_9_out, Func[4]);
  not not_10 (not_10_out, Func[2]);
  not not_11 (not_11_out, Func[1]);
  not not_12 (not_12_out, Func[0]);
  and addu (out_3, r, Func[5], not_9_out, not_8_out, not_10_out, not_11_out, Func[0]);
  and subu (out_4, r, Func[5], not_9_out, not_8_out, not_10_out, Func[1], Func[0]);
  and jr (out_5, r, not_7_out, not_9_out, Func[3], not_10_out, not_11_out, not_12_out);
  and nop (out_6, r, not_7_out, not_9_out, not_8_out, not_10_out, not_11_out, not_12_out);
  and sll (out_7, r, not_7_out, not_9_out, not_8_out, not_10_out, not_11_out, not_12_out);

  // Other names for the same wires on the sheet: addiu = out_14; addu = out_3; beq = out_12; bne = out_15; j = out_11;
  //   jal = out_13; jr = out_5; lb = out_17; lh = out_18; lui = out_16; lw = out_8; nop = out_6; ori = out_10;
  //   sb = out_19; sh = out_20; sll = out_7; subu = out_4; sw = out_9
endmodule

module NpcOp (
  input  beq,
  input  j,
  input  jal,
  input  jr,
  output [2:0] out_5
);

  wire or_1_out;
  wire [2:0] multiplexer_1_out, multiplexer_2_out, multiplexer_3_out;

  Multiplexer #(.width(3), .enable("false")) multiplexer_1 (
    .in0(3'b000), .in1(3'b001), .out(multiplexer_1_out), .sel(beq));
  Multiplexer #(.width(3), .enable("false")) multiplexer_2 (
    .in0(3'b000), .in1(3'b010), .out(multiplexer_2_out), .sel(or_1_out));
  or or_1 (or_1_out, j, jal);
  Multiplexer #(.width(3), .enable("false")) multiplexer_3 (
    .in0(3'b000), .in1(3'b011), .out(multiplexer_3_out), .sel(jr));
  assign out_5 = multiplexer_1_out | multiplexer_2_out | multiplexer_3_out;  // OR_Gate or_2, 3 bits wide
endmodule

module D (
  input  [31:0] Instr_D,
  output [4:0] S1_D,
  output [4:0] S2_D,
  output [1:0] tuse1_D,
  output [1:0] tuse2_D
);

  wire addiu, addu, beq, bne, j, jal, jr, lb, lh, lui, lw, nop, or_1_out, or_2_out, or_3_out, or_4_out,
       or_5_out, or_6_out, or_7_out, or_8_out, or_9_out, or_10_out, or_11_out, or_12_out, or_13_out,
       or_14_out, or_15_out, ori, S1_D_2_out, S1_D_out, sb, sh, sll, subu, sw, tuse1_D_out, tuse2_D_out;
  wire [1:0] bit_extender_1_out;
  wire [4:0] splitter_1__20_16, splitter_1__25_21;
  wire [5:0] splitter_1__5_0, splitter_1__31_26;

  splitter splitter_1 (
    .in_1(Instr_D), ._31_26(splitter_1__31_26), ._5_0(splitter_1__5_0), ._25_21(splitter_1__25_21),
    ._20_16(splitter_1__20_16));  // open: _15_11, out_7, out_8
  or or_1 (or_1_out, lw, sw);
  or or_2 (or_2_out, lb, sb);
  or or_3 (or_3_out, lh, sh);
  or or_4 (or_4_out, or_1_out, or_2_out, or_3_out);
  control_part control_part_1 (
    .out_3(addu), .out_4(subu), .out_5(jr), .out_6(nop), .out_8(lw), .out_9(sw), .out_10(ori), .out_11(j),
    .out_12(beq), .out_13(jal), .out_14(addiu), .out_15(bne), .out_16(lui), .out_17(lb), .out_18(lh),
    .out_19(sb), .out_20(sh), .OP(splitter_1__31_26), .Func(splitter_1__5_0), .out_7(sll));
  or or_5 (or_5_out, addu, subu);
  or or_6 (or_6_out, addiu, ori);
  or or_7 (or_7_out, sw, sb, sh);
  or u_tuse1_D (tuse1_D_out, or_5_out, or_4_out, or_6_out);
  or u_S1_D (S1_D_out, or_7_out, addu, subu, sll, beq);
  Multiplexer #(.width(2), .enable("false")) multiplexer_1 (.in0(2'b00), .in1(2'b01), .out(tuse1_D), .sel(tuse1_D_out));
  or u_tuse2_D (tuse2_D_out, addu, sll, subu);
  Multiplexer #(.width(5), .enable("false")) multiplexer_2 (
    .in0({5{1'b0}}), .in1(splitter_1__25_21), .out(S1_D), .sel(S1_D_2_out));
  Multiplexer #(.width(5), .enable("false")) multiplexer_3 (
    .in0({5{1'b0}}), .in1(splitter_1__20_16), .out(S2_D), .sel(S1_D_out));
  assign bit_extender_1_out = {{1{1'b0}}, tuse2_D_out};  // Bit_Extender bit_extender_1
  or or_8 (or_8_out, lw, sw);
  or or_9 (or_9_out, lb, sb);
  or or_10 (or_10_out, lh, sh);
  or or_11 (or_11_out, sw, sb, sh);
  Multiplexer #(.width(2), .enable("false")) multiplexer_4 (
    .in0(bit_extender_1_out), .in1(2'b10), .out(tuse2_D), .sel(or_11_out));
  or or_12 (or_12_out, or_8_out, or_9_out, or_10_out);
  or or_13 (or_13_out, addu, subu);
  or or_14 (or_14_out, addiu, ori);
  buf or_15 (or_15_out, beq);  // OR_Gate
  or S1_D_2 (S1_D_2_out, or_13_out, or_12_out, or_14_out, or_15_out);
endmodule

module E (
  input  [31:0] Instr_D,
  input  [31:0] extresult,
  input  [31:0] pc_8,
  output [4:0] S1_E,
  output [4:0] S2_E,
  output [3:0] Tnew_E,
  output [4:0] des_E,
  output [31:0] EtoD
);

  wire addiu, addu, beq, bne, j, jal, jr, lb, lh, lui, lw, nop, or_1_out, or_4_out, or_5_out, or_6_out,
       or_7_out, or_8_out, or_9_out, or_10_out, or_11_out, or_14_out, or_15_out, or_16_out, or_17_out,
       or_18_out, or_19_out, ori, S1_E_out, S2_E_out, sb, sh, sll, subu, sw;
  wire [1:0] multiplexer_2_out, multiplexer_3_out, multiplexer_4_out, multiplexer_5_out, multiplexer_6_out,
       or_2_out, or_12_out, or_13_out;
  wire [4:0] rd, rt, splitter_1__25_21;
  wire [5:0] splitter_1__5_0, splitter_1__31_26;

  splitter splitter_1 (
    .in_1(Instr_D), ._31_26(splitter_1__31_26), ._5_0(splitter_1__5_0), ._25_21(splitter_1__25_21),
    ._20_16(rt), ._15_11(rd));  // open: out_7, out_8
  control_part control_part_1 (
    .out_3(addu), .out_4(subu), .out_5(jr), .out_6(nop), .out_8(lw), .out_9(sw), .out_10(ori), .out_11(j),
    .out_12(beq), .out_13(jal), .out_14(addiu), .out_15(bne), .out_16(lui), .out_17(lb), .out_18(lh),
    .out_19(sb), .out_20(sh), .OP(splitter_1__31_26), .Func(splitter_1__5_0), .out_7(sll));
  or or_1 (or_1_out, lw, lb, lh);
  buf or_2 (or_2_out[0], lui);  // OR_Gate
  buf or_3 (or_2_out[1], jal);  // OR_Gate
  or or_4 (or_4_out, addiu, ori);
  Multiplexer #(.select(2), .width(32), .enable("false")) multiplexer_1 (
    .in0({32{1'b0}}), .in1(extresult), .in2(pc_8), .out(EtoD), .sel(or_2_out));  // open: in3
  or or_5 (or_5_out, sw, sb, sh);
  or or_6 (or_6_out, addu, sll, subu);
  or or_7 (or_7_out, addiu, lui, ori);
  or or_8 (or_8_out, lui, or_4_out, or_1_out);
  or or_9 (or_9_out, addu, subu, sll);
  or u_S2_E (S2_E_out, or_5_out, addu, subu, sll);
  or or_10 (or_10_out, or_6_out, or_7_out);
  or or_11 (or_11_out, lw, lb, lh);
  Multiplexer #(.width(2), .enable("false")) multiplexer_2 (
    .in0(2'b00), .in1(2'b01), .out(multiplexer_2_out), .sel(or_8_out));
  Multiplexer #(.width(2), .enable("false")) multiplexer_3 (
    .in0(2'b00), .in1(2'b10), .out(multiplexer_3_out), .sel(or_9_out));
  Multiplexer #(.width(2), .enable("false")) multiplexer_4 (
    .in0(2'b00), .in1(2'b11), .out(multiplexer_4_out), .sel(jal));
  Multiplexer #(.width(2), .enable("false")) multiplexer_5 (
    .in0(2'b00), .in1(2'b01), .out(multiplexer_5_out), .sel(or_10_out));
  Multiplexer #(.width(2), .enable("false")) multiplexer_6 (
    .in0(2'b00), .in1(2'b10), .out(multiplexer_6_out), .sel(or_11_out));
  Multiplexer #(.width(5), .enable("false")) multiplexer_7 (
    .in0({5{1'b0}}), .in1(splitter_1__25_21), .out(S1_E), .sel(S1_E_out));
  Multiplexer #(.width(5), .enable("false")) multiplexer_8 (.in0({5{1'b0}}), .in1(rt), .out(S2_E), .sel(S2_E_out));
  assign or_12_out = multiplexer_2_out | multiplexer_3_out | multiplexer_4_out;  // OR_Gate or_12, 2 bits wide
  assign or_13_out = multiplexer_5_out | multiplexer_6_out;  // OR_Gate or_13, 2 bits wide
  Multiplexer #(.select(2), .width(5)) multiplexer_9 (
    .in0({5{1'b0}}), .in1(rt), .in2(rd), .in3({5{1'b1}}), .out(des_E), .sel(or_12_out));  // open: en
  // Probe on des_E
  or or_14 (or_14_out, lw, sw);
  or or_15 (or_15_out, lb, sb);
  or or_16 (or_16_out, lh, sh);
  assign Tnew_E = {{2{1'b0}}, or_13_out};  // Bit_Extender bit_extender_1
  or or_17 (or_17_out, or_14_out, or_15_out, or_16_out);
  or or_18 (or_18_out, addu, subu);
  or or_19 (or_19_out, addiu, ori);
  or u_S1_E (S1_E_out, or_18_out, or_17_out, or_19_out);

  // Notes on the sheet:
  //   这里可能有问题
  //   WRSel(M1)(RegDst)
endmodule

module M (
  input  [31:0] Instr_D,
  input  [31:0] aluresult,
  input  [31:0] pc_8,
  output [4:0] S2_E,
  output [4:0] des_E,
  output [31:0] EtoD
);

  wire addiu, addu, beq, bne, j, jal, jr, lb, lh, lui, lw, nop, or_1_out, or_2_out, or_3_out, or_4_out,
       or_5_out, or_6_out, or_7_out, ori, S2_E_out, sb, sh, sll, subu, sw;
  wire [1:0] multiplexer_1_out, multiplexer_2_out, multiplexer_3_out, or_9_out, or_10_out;
  wire [4:0] rd, rt;
  wire [5:0] splitter_1__5_0, splitter_1__31_26;

  splitter splitter_1 (
    .in_1(Instr_D), ._31_26(splitter_1__31_26), ._5_0(splitter_1__5_0), ._20_16(rt), ._15_11(rd));  // open: _25_21, out_7, out_8
  or or_1 (or_1_out, lw, lb, lh);
  control_part control_part_1 (
    .out_3(addu), .out_4(subu), .out_5(jr), .out_6(nop), .out_8(lw), .out_9(sw), .out_10(ori), .out_11(j),
    .out_12(beq), .out_13(jal), .out_14(addiu), .out_15(bne), .out_16(lui), .out_17(lb), .out_18(lh),
    .out_19(sb), .out_20(sh), .OP(splitter_1__31_26), .Func(splitter_1__5_0), .out_7(sll));
  or or_2 (or_2_out, addiu, ori);
  or or_3 (or_3_out, addiu, ori);
  or or_4 (or_4_out, addu, sll, subu);
  or or_5 (or_5_out, lui, or_3_out);
  or or_6 (or_6_out, lui, or_2_out, or_1_out);
  or or_7 (or_7_out, addu, subu, sll);
  buf or_8 (or_9_out[1], jal);  // OR_Gate
  or or_9 (or_9_out[0], or_4_out, or_5_out);
  Multiplexer #(.width(2), .enable("false")) multiplexer_1 (
    .in0(2'b00), .in1(2'b10), .out(multiplexer_1_out), .sel(or_7_out));
  Multiplexer #(.width(2), .enable("false")) multiplexer_2 (
    .in0(2'b00), .in1(2'b11), .out(multiplexer_2_out), .sel(jal));
  Multiplexer #(.width(2), .enable("false")) multiplexer_3 (
    .in0(2'b00), .in1(2'b01), .out(multiplexer_3_out), .sel(or_6_out));
  Multiplexer #(.select(2), .width(32), .enable("false")) multiplexer_4 (
    .in0({32{1'b0}}), .in1(aluresult), .in2(pc_8), .out(EtoD), .sel(or_9_out));  // open: in3
  or u_S2_E (S2_E_out, sw, sh, sb);
  Multiplexer #(.select(2), .width(5)) multiplexer_5 (
    .in0({5{1'b0}}), .in1(rt), .in2(rd), .in3({5{1'b1}}), .out(des_E), .sel(or_10_out));  // open: en
  assign or_10_out = multiplexer_3_out | multiplexer_1_out | multiplexer_2_out;  // OR_Gate or_10, 2 bits wide
  Multiplexer #(.width(5), .enable("false")) multiplexer_6 (.in0({5{1'b0}}), .in1(rt), .out(S2_E), .sel(S2_E_out));
  // Probe on des_E

  // Notes on the sheet:
  //   WRSel(M1)(RegDst)
endmodule

module W (
  input  [31:0] Instr_D,
  input  [31:0] aluresult,
  input  [31:0] pc_8,
  input  [31:0] RegData,
  output [4:0] des_E,
  output [31:0] EtoD
);

  wire addiu, addu, beq, bne, j, jal, jr, lb, lh, lui, lw, nop, or_1_out, or_2_out, or_3_out, or_4_out,
       or_5_out, or_6_out, or_8_out, or_9_out, ori, sb, sh, sll, subu, sw;
  wire [1:0] multiplexer_1_out, multiplexer_2_out, multiplexer_3_out, or_12_out;
  wire [2:0] or_10_out;
  wire [4:0] rd, rt;
  wire [5:0] splitter_1__5_0, splitter_1__31_26;

  splitter splitter_1 (
    .in_1(Instr_D), ._31_26(splitter_1__31_26), ._5_0(splitter_1__5_0), ._20_16(rt), ._15_11(rd));  // open: _25_21, out_7, out_8
  or or_1 (or_1_out, lw, lb, lh);
  or or_2 (or_2_out, addiu, ori);
  or or_3 (or_3_out, addiu, ori);
  control_part control_part_1 (
    .out_3(addu), .out_4(subu), .out_5(jr), .out_6(nop), .out_8(lw), .out_9(sw), .out_10(ori), .out_11(j),
    .out_12(beq), .out_13(jal), .out_14(addiu), .out_15(bne), .out_16(lui), .out_17(lb), .out_18(lh),
    .out_19(sb), .out_20(sh), .OP(splitter_1__31_26), .Func(splitter_1__5_0), .out_7(sll));
  or or_4 (or_4_out, lw, lb, lh);
  or or_5 (or_5_out, lui, or_2_out, or_1_out);
  or or_6 (or_6_out, addu, subu, sll);
  buf or_7 (or_10_out[1], jal);  // OR_Gate
  or or_8 (or_8_out, addu, sll, subu);
  or or_9 (or_9_out, lui, or_3_out);
  Multiplexer #(.width(2), .enable("false")) multiplexer_1 (
    .in0(2'b00), .in1(2'b01), .out(multiplexer_1_out), .sel(or_5_out));
  Multiplexer #(.width(2), .enable("false")) multiplexer_2 (
    .in0(2'b00), .in1(2'b10), .out(multiplexer_2_out), .sel(or_6_out));
  Multiplexer #(.width(2), .enable("false")) multiplexer_3 (
    .in0(2'b00), .in1(2'b11), .out(multiplexer_3_out), .sel(jal));
  or or_10 (or_10_out[0], or_8_out, or_9_out);
  buf or_11 (or_10_out[2], or_4_out);  // OR_Gate
  assign or_12_out = multiplexer_1_out | multiplexer_2_out | multiplexer_3_out;  // OR_Gate or_12, 2 bits wide
  Multiplexer #(.select(3), .width(32), .enable("false")) multiplexer_4 (
    .in0({32{1'b0}}), .in1(aluresult), .in2(pc_8), .in4(RegData), .out(EtoD), .sel(or_10_out));  // open: in3, in5, in6, in7
  Multiplexer #(.select(2), .width(5)) multiplexer_5 (
    .in0({5{1'b0}}), .in1(rt), .in2(rd), .in3({5{1'b1}}), .out(des_E), .sel(or_12_out));  // open: en
  // Probe on des_E

  // Notes on the sheet:
  //   WRSel(M1)(RegDst)
endmodule
